# Fritzing sketch FritzingDiagaram (saved by Fritzing 0.9.10b)
breadboards: 1

parts:
  R1 = Trimmer Potentiometer [maximum_resistance=10kΩ knob_status=50% power=0.5W package=THT]
  R2 = Trimmer Potentiometer [maximum_resistance=10kΩ knob_status=50% power=0.5W package=THT]
  R3 = Trimmer Potentiometer [maximum_resistance=10kΩ knob_status=50% power=0.5W package=THT]
  R4 = Trimmer Potentiometer [maximum_resistance=10kΩ knob_status=50% power=0.5W package=THT]
  R5 = Trimmer Potentiometer [maximum_resistance=10kΩ knob_status=50% power=0.5W package=THT]
  R6 = Trimmer Potentiometer [maximum_resistance=10kΩ knob_status=50% power=0.5W package=THT]
  M1 = Nucleo 144 MB1137
  BT1 = Bluetooth HC-06u [package=THT]
  part = Basic Force Sensing Resistor (FSR) [package=THT]
  J2 = Basic Force Sensing Resistor (FSR) [package=THT]
  J4 = Basic Force Sensing Resistor (FSR) [package=THT]
  J5 = Basic Force Sensing Resistor (FSR) [package=THT]
  J6 = Basic Force Sensing Resistor (FSR) [package=THT]
  part_2 = Basic Force Sensing Resistor (FSR) [package=THT]
  C1 = Ceramic Capacitor [capacitance=100nF voltage=35V package="100 mil [THT, multilayer]"]

nets:
  N1: R1.leg1, M1.SPI_A_SCK/PA5, M1.PA5, part.pin_0
  N2: R2.leg1, M1.SPI_A_MISO_/PA6, M1.PA6, part_2.pin_0
  N3: R3.leg1, M1.SPI_A_MOSI/PA7, M1.PA7, J2.pin_0
  GND: R4.leg1, M1.GND, M1.PE2, M1.ADC_A_IN/PB1, BT1.GND, J5.pin_0, C1.0
  N4: R5.leg1, M1.PC3, M1.A2/PC3, J4.pin_0
  N5: R6.leg1, M1.PC0, M1.A1/PC0, J6.pin_0
  N6: M1.+3.3V, part.pin_1, J2.pin_1, J4.pin_1, J5.pin_1, J6.pin_1, part_2.pin_1
  +5V: M1.+5V, BT1.VCC
  N7: M1.PD5, M1.USART_B_TX/PD5, BT1.RXD
  N8: M1.PD6, M1.USART_B_RX/PD6, BT1.TXD

notes:
  HC-06 Bluetooth Module NOTE:
  Needs 5V fail but logic is 3.3
  STM32-767ZI
  NOTE: logic outputs at 3.3V
  6 Variable Resistors 1-20k
  Force Sensor PA5 LU
  Force Sensor PA6 RL
  Force Sensor PA7
  Bdy (chest Guard)
  Force Sensor PB1
  RU
  Force Sensor PC3
  Hd.
  NOTE: This sensor is comprised of four force sensors that are wired in parallel. Each at one corner of the facegaurd
  Force Sensor PC0 LL
  Decoupling capacitor

custom parts:
  Nucleo 144 MB1137: The STM32 Nucleo-144 boards based on the MB1137 reference board (NUCLEO-F207ZG, NUCLEO-F303ZE, NUCLEO-F412ZG, NUCLEO-F413ZH, NUCLEO-F429ZI, NUCLEO-F439ZI, NUCLEO-F446ZE, NUCLEO-F722ZE, NUCLEO-F746ZG, NUCLEO-F756ZG, NUCLEO-F767ZI and NUCLEO-H743ZI) provide an affordable and flexible way for users to try out new concepts and build prototypes with STM32 microcontrollers.
  Bluetooth HC-06u: Bluetooth HC-06 - face up, pins down 16.5mm x 37.5mm PCB
